// Logisim project proj_2_2.circ as structural Verilog: 17 circuits, main circuit testbench
module inst_fetch (
  input  clk,
  input  rst,
  input  control_en_i,
  input  [31:0] control_pc_i,
  input  [15:0] inst_i,
  output inst_en_o,
  output [31:0] current_pc_o,
  output [31:0] inst_addr_o,
  output [15:0] inst_o
);

  wire not_1_out, not_2_out;
  wire [31:0] adder_1_out, counter_1_q, multiplexer_1_out;

  not not_1 (not_1_out, rst);
  Adder #(.width(32)) adder_1 (.a(control_pc_i), .b(32'h1), .out(adder_1_out));  // open: cin, cout
  Counter #(.max('hffffffff), .width(32)) counter_1 (
    .clr(rst), .load(control_en_i), .up(not_1_out), .count(not_1_out), .clk(clk), .D(adder_1_out),
    .Q(counter_1_q));  // open: carry
  Multiplexer #(.width(32)) multiplexer_1 (
    .in0(counter_1_q), .in1(control_pc_i), .out(multiplexer_1_out), .sel(control_en_i));
  not not_2 (not_2_out, rst);
  Register #(.width(32)) register_1 (.D(multiplexer_1_out), .en(not_2_out), .clk(clk), .Q(current_pc_o), .clr(rst));
  not not_3 (inst_en_o, rst);

  assign inst_addr_o = current_pc_o;
  assign inst_o = inst_i;

  // Notes on the sheet:
  //   Don't touch
endmodule

module TOP (
  input  rst,
  input  clk,
  input  [15:0] inst,
  input  [31:0] mem_result,
  input  [31:0] current_pc,
  output out_6,
  output [31:0] mem_din,
  output mem_ren,
  output [31:0] alu_result,
  output control_en,
  output [31:0] control_pc,
  output wb_en,
  output [4:0] wb_addr,
  output [31:0] wb_data
);

  wire comparator_1_eq, memory_read_enable_1_enable, memory_write_enable_1_enable, not_1_out, or_1_out,
       pc_write_enable_1_enable, register_write_enable_1_enable, rs2_or_imm_1_data_2_choose;
  wire [4:0] register_address_1_reg_address, register_fetch_1_rd, register_fetch_1_rs1, register_fetch_1_rs2;
  wire [31:0] alu_file_1_alu_result, imm_gen_1_imm, memory_address_1_mem_addr, memory_data_1_mem_data,
       multiplexer_1_out, pc_data_1_pc_out, register_file_1_rd_data, register_file_1_rs1_data,
       register_file_1_rs2_data, register_file_1_x2_data, register_write_data_1_out_4;

  register_fetch register_fetch_1 (
    .inst(inst), .rd(register_fetch_1_rd), .rs1(register_fetch_1_rs1), .rs2(register_fetch_1_rs2));
  register_file register_file_1 (
    .read_rd(register_fetch_1_rd), .read_rs2(register_fetch_1_rs2), .read_rs1(register_fetch_1_rs1),
    .data_in(wb_data), .write_enable(wb_en), .write_register(wb_addr), .clk(clk), .rst(rst),
    .rd_data(register_file_1_rd_data), .rs2_data(register_file_1_rs2_data),
    .rs1_data(register_file_1_rs1_data), .x2_data(register_file_1_x2_data));
  rs2_or_imm rs2_or_imm_1 (.inst(inst), .data_2_choose(rs2_or_imm_1_data_2_choose));
  imm_gen imm_gen_1 (.inst(inst), .imm(imm_gen_1_imm));
  Multiplexer #(.width(32)) multiplexer_1 (
    .in0(register_file_1_rs2_data), .in1(imm_gen_1_imm), .out(multiplexer_1_out),
    .sel(rs2_or_imm_1_data_2_choose));
  Comparator #(.width(16)) comparator_1 (.a(inst), .b(16'h8000), .eq(comparator_1_eq));  // open: gt, lt
  or or_1 (or_1_out, comparator_1_eq, rst);
  not not_1 (not_1_out, or_1_out);
  alu_file alu_file_1 (
    .data_rd(register_file_1_rd_data), .data_2(multiplexer_1_out), .rs1(register_file_1_rs1_data),
    .x2(register_file_1_x2_data), .mem_result(mem_result), .inst(inst), .alu_result(alu_file_1_alu_result));
  register_write_enable register_write_enable_1 (
    .inst(inst), .data_rs2(register_file_1_rs2_data), .enable(register_write_enable_1_enable));
  register_address register_address_1 (
    .data_rs2(register_file_1_rs2_data), .inst(inst), .rd(register_fetch_1_rd),
    .reg_address(register_address_1_reg_address));
  register_write_data register_write_data_1 (
    .data_rs2(register_file_1_rs2_data), .inst(inst), .alu_result(alu_file_1_alu_result),
    .out_4(register_write_data_1_out_4));
  memory_write_enable memory_write_enable_1 (.inst(inst), .enable(memory_write_enable_1_enable));
  memory_data memory_data_1 (.rs2(register_file_1_rs2_data), .inst(inst), .mem_data(memory_data_1_mem_data));
  memory_read_enable memory_read_enable_1 (.inst(inst), .enable(memory_read_enable_1_enable));
  memory_address memory_address_1 (
    .inst(inst), .alu_result(alu_file_1_alu_result), .mem_addr(memory_address_1_mem_addr));
  pc_write_enable pc_write_enable_1 (
    .inst(inst), .rs1(register_file_1_rs1_data), .rs2(register_file_1_rs2_data),
    .enable(pc_write_enable_1_enable));
  pc_data pc_data_1 (
    .inst(inst), .pc_in(current_pc), .data_rs1(register_file_1_rs1_data),
    .data_rs2(register_file_1_rs2_data), .data_imm(imm_gen_1_imm), .pc_out(pc_data_1_pc_out));
  Multiplexer multiplexer_2 (.in0(1'b0), .in1(register_write_enable_1_enable), .out(wb_en), .sel(not_1_out));
  Multiplexer #(.width(5)) multiplexer_3 (
    .in0({5{1'b0}}), .in1(register_address_1_reg_address), .out(wb_addr), .sel(not_1_out));
  Multiplexer #(.width(32)) multiplexer_4 (
    .in0({32{1'b0}}), .in1(register_write_data_1_out_4), .out(wb_data), .sel(not_1_out));
  Multiplexer multiplexer_5 (.in0(1'b0), .in1(memory_write_enable_1_enable), .out(out_6), .sel(not_1_out));
  Multiplexer #(.width(32)) multiplexer_6 (
    .in0({32{1'b0}}), .in1(memory_data_1_mem_data), .out(mem_din), .sel(not_1_out));
  Multiplexer multiplexer_7 (.in0(1'b0), .in1(memory_read_enable_1_enable), .out(mem_ren), .sel(not_1_out));
  Multiplexer #(.width(32)) multiplexer_8 (
    .in0({32{1'b0}}), .in1(memory_address_1_mem_addr), .out(alu_result), .sel(not_1_out));
  Multiplexer multiplexer_9 (.in0(1'b0), .in1(pc_write_enable_1_enable), .out(control_en), .sel(not_1_out));
  Multiplexer #(.width(32)) multiplexer_10 (
    .in0({32{1'b0}}), .in1(pc_data_1_pc_out), .out(control_pc), .sel(not_1_out));

  // Other names for the same wires on the sheet: mem_wen = out_6

  // Notes on the sheet:
  //   Fixed I/O
  //   Don't touch
endmodule

module testbench (
  input  rst,
  output mem_wen,
  output [31:0] mem_din,
  output mem_ren,
  output [31:0] mem_addr,
  output control_en,
  output [31:0] control_pc,
  output halt,
  output wb_en,
  output [4:0] wb_addr,
  output [31:0] wb_data
);

  wire clk, inst_en, not_1_out, not_2_out, not_3_out, not_4_out, por_1_out, rst_t;
  wire [15:0] inst, inst_i;
  wire [31:0] current_pc, inst_addr, mem_result;

  not not_1 (not_1_out, inst_i[0]);
  not not_2 (not_2_out, inst_i[1]);
  not not_3 (not_3_out, inst_i[13]);
  not not_4 (not_4_out, inst_i[14]);
  and and_1 (halt, not_1_out, not_2_out, not_3_out, not_4_out, inst_i[15]);
  Clock clock_1 (.out(clk));
  or or_1 (rst_t, rst, por_1_out);
  POR por_1 (.out(por_1_out));
  inst_fetch inst_fetch_1 (
    .clk(clk), .rst(rst_t), .control_en_i(control_en), .control_pc_i(control_pc), .inst_i(inst_i),
    .inst_en_o(inst_en), .current_pc_o(current_pc), .inst_addr_o(inst_addr), .inst_o(inst));
  TOP top_1 (
    .rst(rst_t), .clk(clk), .inst(inst), .mem_result(mem_result), .current_pc(current_pc), .out_6(mem_wen),
    .mem_din(mem_din), .mem_ren(mem_ren), .alu_result(mem_addr), .control_en(control_en),
    .control_pc(control_pc), .wb_en(wb_en), .wb_addr(wb_addr), .wb_data(wb_data));
  ROM #(.dataWidth(16)) rom_1 (.addr(inst_addr[7:0]), .data(inst_i));
  RAM #(.addrWidth(16), .asyncread("true"), .clearpin("true"), .dataWidth(32), .\type ("nonvolatile")) ram_1 (
    .addr(mem_addr[15:0]), .we(mem_wen), .oe(mem_ren), .clk(clk), .din(mem_din), .dout(mem_result),
    .clr(rst_t));

  // Notes on the sheet:
  //   contents of rom_1 (hex, n*v repeats v):
  //   4409 147d c011 bffd 1 1 4111 5429 c422 44b5 48 8482 8526 414c 511 c148 8000
  //   you can write any instruction in
endmodule

module register_file (
  input  [4:0] read_rd,
  input  [4:0] read_rs2,
  input  [4:0] read_rs1,
  input  [31:0] data_in,
  input  write_enable,
  input  [4:0] write_register,
  input  clk,
  input  rst,
  output [31:0] rd_data,
  output [31:0] rs2_data,
  output [31:0] rs1_data,
  output [31:0] x2_data
);

  wire demultiplexer_1_out2, demultiplexer_1_out8, demultiplexer_1_out9, demultiplexer_1_out10,
       demultiplexer_1_out11, demultiplexer_1_out12, demultiplexer_1_out13, demultiplexer_1_out14,
       demultiplexer_1_out15;
  wire [31:0] x0_q, x8_q, x9_q, x10_q, x11_q, x12_q, x13_q, x14_q, x15_q;

  Demultiplexer #(.select(5)) demultiplexer_1 (
    .out2(demultiplexer_1_out2), .out8(demultiplexer_1_out8), .out9(demultiplexer_1_out9),
    .out10(demultiplexer_1_out10), .out11(demultiplexer_1_out11), .out12(demultiplexer_1_out12),
    .out13(demultiplexer_1_out13), .out14(demultiplexer_1_out14), .out15(demultiplexer_1_out15),
    .in(write_enable), .sel(write_register));  // open: out0, out1, out3, out4, out5, out6, out7, out16, out17, out18, out19, out20, out21, out22, out23, out24, out25, out26, out27, out28, out29, out30, out31
  Register #(.width(32)) x0 (.en(1'b0), .clk(clk), .Q(x0_q), .clr(rst));  // open: D
  Register #(.width(32)) x2 (.D(data_in), .en(demultiplexer_1_out2), .clk(clk), .Q(x2_data), .clr(rst));
  Register #(.width(32)) x8 (.D(data_in), .en(demultiplexer_1_out8), .clk(clk), .Q(x8_q), .clr(rst));
  Register #(.width(32)) x9 (.D(data_in), .en(demultiplexer_1_out9), .clk(clk), .Q(x9_q), .clr(rst));
  Register #(.width(32)) x10 (.D(data_in), .en(demultiplexer_1_out10), .clk(clk), .Q(x10_q), .clr(rst));
  Register #(.width(32)) x11 (.D(data_in), .en(demultiplexer_1_out11), .clk(clk), .Q(x11_q), .clr(rst));
  Register #(.width(32)) x12 (.D(data_in), .en(demultiplexer_1_out12), .clk(clk), .Q(x12_q), .clr(rst));
  Register #(.width(32)) x13 (.D(data_in), .en(demultiplexer_1_out13), .clk(clk), .Q(x13_q), .clr(rst));
  Register #(.width(32)) x14 (.D(data_in), .en(demultiplexer_1_out14), .clk(clk), .Q(x14_q), .clr(rst));
  Register #(.width(32)) x15 (.D(data_in), .en(demultiplexer_1_out15), .clk(clk), .Q(x15_q), .clr(rst));
  Multiplexer #(.select(5), .width(32)) multiplexer_1 (
    .in0(x0_q), .in2(x2_data), .in8(x8_q), .in9(x9_q), .in10(x10_q), .in11(x11_q), .in12(x12_q),
    .in13(x13_q), .in14(x14_q), .in15(x15_q), .out(rd_data), .sel(read_rd));  // open: in1, in3, in4, in5, in6, in7, in16, in17, in18, in19, in20, in21, in22, in23, in24, in25, in26, in27, in28, in29, in30, in31
  Multiplexer #(.select(5), .width(32)) multiplexer_2 (
    .in0(x0_q), .in2(x2_data), .in8(x8_q), .in9(x9_q), .in10(x10_q), .in11(x11_q), .in12(x12_q),
    .in13(x13_q), .in14(x14_q), .in15(x15_q), .out(rs2_data), .sel(read_rs2));  // open: in1, in3, in4, in5, in6, in7, in16, in17, in18, in19, in20, in21, in22, in23, in24, in25, in26, in27, in28, in29, in30, in31
  Multiplexer #(.select(5), .width(32)) multiplexer_3 (
    .in0(x0_q), .in2(x2_data), .in8(x8_q), .in9(x9_q), .in10(x10_q), .in11(x11_q), .in12(x12_q),
    .in13(x13_q), .in14(x14_q), .in15(x15_q), .out(rs1_data), .sel(read_rs1));  // open: in1, in3, in4, in5, in6, in7, in16, in17, in18, in19, in20, in21, in22, in23, in24, in25, in26, in27, in28, in29, in30, in31

  // Other names for the same wires on the sheet: read_data[31:0] = rd_data; read_data_1[31:0] = rs1_data;
  //   read_data_2[31:0] = rs2_data; read_register[4:0] = read_rd; read_register_1[4:0] = read_rs1;
  //   read_register_2[4:0] = read_rs2; x2[31:0] = x2_data
endmodule

module alu_file (
  input  [31:0] data_rd,
  input  [31:0] data_2,
  input  [31:0] rs1,
  input  [31:0] x2,
  input  [31:0] mem_result,
  input  [15:0] inst,
  output [31:0] alu_result
);

  wire [31:0] adder_1_out, adder_2_out, adder_3_out, multiplexer_1_out, shifter_1_out;

  Adder #(.width(32)) adder_1 (.a(data_rd), .b(data_2), .out(adder_1_out));  // open: cin, cout
  Adder #(.width(32)) adder_2 (.a(data_2), .b(rs1), .out(adder_2_out));  // open: cin, cout
  Shifter #(.width(32)) shifter_1 (.in(data_rd), .\dist (data_2[4:0]), .out(shifter_1_out));
  Adder #(.width(32)) adder_3 (.a(data_2), .b(x2), .out(adder_3_out));  // open: cin, cout
  Adder adder_4 ();  // open: a, b, out, cin, cout
  Multiplexer #(.width(32)) multiplexer_1 (.in0(data_2), .in1(adder_1_out), .out(multiplexer_1_out), .sel(inst[12]));
  Multiplexer #(.select(5), .width(32)) multiplexer_2 (
    .in0(adder_3_out), .in1(adder_1_out), .in2(shifter_1_out), .in8(mem_result), .in9(data_2), .in13(data_2),
    .in18(multiplexer_1_out), .in24(adder_2_out), .in26(adder_3_out), .out(alu_result),
    .sel({inst[15:13], inst[1:0]}));  // open: in3, in4, in5, in6, in7, in10, in11, in12, in14, in15, in16, in17, in19, in20, in21, in22, in23, in25, in27, in28, in29, in30, in31

  // Other names for the same wires on the sheet: data_mem[31:0] = mem_result
endmodule

module imm_gen (
  input  [15:0] inst,
  output [31:0] imm
);

  wire [0:0] undriven_4, undriven_5;
  wire [1:0] undriven, undriven_2, undriven_3;
  wire [31:0] bit_extender_1_out, bit_extender_2_out, bit_extender_3_out, bit_extender_4_out,
       bit_extender_5_out, bit_extender_6_out, shifter_1_out;

  assign bit_extender_1_out = {{26{inst[12]}}, {inst[12], inst[6:2]}};  // Bit_Extender bit_extender_1
  assign bit_extender_2_out = {{25{inst[5]}}, {inst[5], inst[12:10], inst[6], undriven}};  // Bit_Extender bit_extender_2
  assign bit_extender_3_out = {{24{inst[8]}}, {inst[8:7], inst[12:9], undriven_2}};  // Bit_Extender bit_extender_3
  assign bit_extender_4_out = {{22{inst[10]}}, {inst[10:7], inst[12:11], inst[5], inst[6], undriven_3}};  // Bit_Extender bit_extender_4
  assign bit_extender_5_out = {{20{inst[12]}}, {inst[12], inst[8], inst[10:9], inst[6], inst[7], inst[2], inst[11], inst[5:3], undriven_4[0]}};  // Bit_Extender bit_extender_5
  assign bit_extender_6_out = {{23{inst[12]}}, {inst[12], inst[8:7], inst[3], inst[11:10], inst[6], inst[4], undriven_5[0]}};  // Bit_Extender bit_extender_6
  Shifter #(.width(32)) shifter_1 (.in(bit_extender_1_out), .\dist (5'b01100), .out(shifter_1_out));
  Multiplexer #(.select(5), .width(32)) multiplexer_1 (
    .in0(bit_extender_4_out), .in1(bit_extender_1_out), .in2(bit_extender_1_out), .in8(bit_extender_2_out),
    .in9(bit_extender_1_out), .in13(shifter_1_out), .in21(bit_extender_5_out), .in24(bit_extender_2_out),
    .in25(bit_extender_6_out), .in26(bit_extender_3_out), .out(imm), .sel({inst[15:13], inst[1:0]}));  // open: in3, in4, in5, in6, in7, in10, in11, in12, in14, in15, in16, in17, in18, in19, in20, in22, in23, in27, in28, in29, in30, in31

  // Notes on the sheet:
  //   CI
endmodule

module rs2_or_imm (
  input  [15:0] inst,
  output data_2_choose
);

  Multiplexer #(.select(5)) multiplexer_1 (
    .in0(1'b1), .in1(1'b1), .in2(1'b1), .in9(1'b1), .in13(1'b1), .in18(1'b0), .in21(1'b1), .in24(1'b1),
    .in26(1'b1), .out(data_2_choose), .sel({inst[15:13], inst[1:0]}));  // open: in3, in4, in5, in6, in7, in8, in10, in11, in12, in14, in15, in16, in17, in19, in20, in22, in23, in25, in27, in28, in29, in30, in31
endmodule

module register_fetch (
  input  [15:0] inst,
  output [4:0] rd,
  output [4:0] rs1,
  output [4:0] rs2
);

  wire [4:0] adder_1_out, adder_2_out, adder_3_out, bit_extender_1_out, bit_extender_2_out,
       bit_extender_3_out;

  assign bit_extender_1_out = {{2{inst[4]}}, inst[4:2]};  // Bit_Extender bit_extender_1
  assign bit_extender_2_out = {{2{inst[9]}}, inst[9:7]};  // Bit_Extender bit_extender_2
  assign bit_extender_3_out = {{2{inst[4]}}, inst[4:2]};  // Bit_Extender bit_extender_3
  Adder #(.width(5)) adder_1 (.a(5'b01000), .b(bit_extender_3_out), .out(adder_1_out));  // open: cin, cout
  Adder #(.width(5)) adder_2 (.a(5'b01000), .b(bit_extender_1_out), .out(adder_2_out));  // open: cin, cout
  Adder #(.width(5)) adder_3 (.a(5'b01000), .b(bit_extender_2_out), .out(adder_3_out));  // open: cin, cout
  Multiplexer #(.select(5), .width(5)) multiplexer_1 (
    .in0(adder_2_out), .in1(inst[11:7]), .in2(inst[11:7]), .in8(adder_2_out), .in9(inst[11:7]),
    .in13(inst[11:7]), .in18(inst[11:7]), .out(rd), .sel({inst[15:13], inst[1:0]}));  // open: in3, in4, in5, in6, in7, in10, in11, in12, in14, in15, in16, in17, in19, in20, in21, in22, in23, in24, in25, in26, in27, in28, in29, in30, in31
  Multiplexer #(.select(5), .width(5)) multiplexer_2 (
    .in8(adder_3_out), .in24(adder_3_out), .in25(adder_3_out), .out(rs1), .sel({inst[15:13], inst[1:0]}));  // open: in0, in1, in2, in3, in4, in5, in6, in7, in9, in10, in11, in12, in13, in14, in15, in16, in17, in18, in19, in20, in21, in22, in23, in26, in27, in28, in29, in30, in31
  Multiplexer #(.select(5), .width(5)) multiplexer_3 (
    .in18(inst[6:2]), .in24(adder_1_out), .in26(inst[6:2]), .out(rs2), .sel({inst[15:13], inst[1:0]}));  // open: in0, in1, in2, in3, in4, in5, in6, in7, in8, in9, in10, in11, in12, in13, in14, in15, in16, in17, in19, in20, in21, in22, in23, in25, in27, in28, in29, in30, in31
endmodule

module register_write_enable (
  input  [15:0] inst,
  input  [31:0] data_rs2,
  output enable
);

  wire comparator_1_eq, multiplexer_1_out;

  Comparator #(.width(32)) comparator_1 (.a({32{1'b0}}), .b(data_rs2), .eq(comparator_1_eq));  // open: gt, lt
  Multiplexer multiplexer_1 (.in0(1'b1), .in1(1'b0), .out(multiplexer_1_out), .sel(comparator_1_eq));
  Multiplexer #(.select(5)) multiplexer_2 (
    .in0(1'b1), .in1(1'b0), .in2(1'b1), .in3(1'b0), .in4(1'b0), .in5(1'b0), .in6(1'b0), .in7(1'b0),
    .in8(1'b1), .in9(1'b0), .in10(1'b1), .in11(1'b1), .in12(1'b0), .in13(1'b0), .in14(1'b0), .in15(1'b0),
    .in16(1'b1), .in17(1'b0), .in18(multiplexer_1_out), .in19(1'b0), .in20(1'b0), .in21(1'b0), .in22(1'b0),
    .in23(1'b0), .in24(1'b0), .in25(1'b0), .in26(1'b0), .in27(1'b0), .in28(1'b0), .in29(1'b0), .in30(1'b0),
    .in31(1'b0), .out(enable), .sel({inst[15:13], inst[1:0]}));

  // Other names for the same wires on the sheet: rs2[31:0] = data_rs2
endmodule

module register_address (
  input  [31:0] data_rs2,
  input  [15:0] inst,
  input  [4:0] rd,
  output [4:0] reg_address
);

  wire comparator_1_eq;
  wire [4:0] multiplexer_1_out;

  Comparator #(.width(32)) comparator_1 (.a({32{1'b0}}), .b(data_rs2), .eq(comparator_1_eq));  // open: gt, lt
  Multiplexer #(.width(5)) multiplexer_1 (.in0(rd), .in1({5{1'b0}}), .out(multiplexer_1_out), .sel(comparator_1_eq));
  Multiplexer #(.select(5), .width(5)) multiplexer_2 (
    .in0(rd), .in1(rd), .in2({5{1'b0}}), .in3({5{1'b0}}), .in4({5{1'b0}}), .in5({5{1'b0}}), .in6({5{1'b0}}),
    .in7({5{1'b0}}), .in8(rd), .in9(rd), .in10({5{1'b0}}), .in11({5{1'b0}}), .in12({5{1'b0}}), .in13(rd),
    .in14({5{1'b0}}), .in15({5{1'b0}}), .in16(rd), .in17({5{1'b0}}), .in18(multiplexer_1_out),
    .in19({5{1'b0}}), .in20({5{1'b0}}), .in21({5{1'b0}}), .in22({5{1'b0}}), .in23({5{1'b0}}),
    .in24({5{1'b0}}), .in25({5{1'b0}}), .in26({5{1'b0}}), .in27({5{1'b0}}), .in28({5{1'b0}}),
    .in29({5{1'b0}}), .in30({5{1'b0}}), .in31({5{1'b0}}), .out(reg_address), .sel({inst[15:13], inst[1:0]}));

  // Other names for the same wires on the sheet: rs2[31:0] = data_rs2
endmodule

module register_write_data (
  input  [31:0] data_rs2,
  input  [15:0] inst,
  input  [31:0] alu_result,
  output [31:0] out_4
);

  wire comparator_1_eq;
  wire [31:0] multiplexer_1_out;

  Comparator #(.width(32)) comparator_1 (.a({32{1'b0}}), .b(data_rs2), .eq(comparator_1_eq));  // open: gt, lt
  Multiplexer #(.width(32)) multiplexer_1 (
    .in0(alu_result), .in1({32{1'b0}}), .out(multiplexer_1_out), .sel(comparator_1_eq));
  Multiplexer #(.select(5), .width(32)) multiplexer_2 (
    .in0(alu_result), .in1({32{1'b0}}), .in2(alu_result), .in3({32{1'b0}}), .in4({32{1'b0}}),
    .in5({32{1'b0}}), .in6({32{1'b0}}), .in7({32{1'b0}}), .in8(alu_result), .in9({32{1'b0}}),
    .in10(alu_result), .in11(alu_result), .in12({32{1'b0}}), .in13({32{1'b0}}), .in14({32{1'b0}}),
    .in15({32{1'b0}}), .in16(alu_result), .in17({32{1'b0}}), .in18(multiplexer_1_out), .in19({32{1'b0}}),
    .in20({32{1'b0}}), .in21({32{1'b0}}), .in22({32{1'b0}}), .in23({32{1'b0}}), .in24({32{1'b0}}),
    .in25({32{1'b0}}), .in26({32{1'b0}}), .in27({32{1'b0}}), .in28({32{1'b0}}), .in29({32{1'b0}}),
    .in30({32{1'b0}}), .in31({32{1'b0}}), .out(out_4), .sel({inst[15:13], inst[1:0]}));

  // Other names for the same wires on the sheet: reg_data[31:0] = out_4; rs2[31:0] = data_rs2
endmodule

module memory_write_enable (
  input  [15:0] inst,
  output enable
);

  Multiplexer #(.select(5)) multiplexer_1 (
    .in0(1'b0), .in1(1'b0), .in2(1'b0), .in3(1'b0), .in4(1'b0), .in5(1'b0), .in6(1'b0), .in7(1'b0),
    .in8(1'b0), .in9(1'b0), .in10(1'b0), .in11(1'b0), .in12(1'b0), .in13(1'b0), .in14(1'b0), .in15(1'b0),
    .in16(1'b0), .in17(1'b0), .in18(1'b0), .in19(1'b0), .in20(1'b0), .in21(1'b0), .in22(1'b0), .in23(1'b0),
    .in24(1'b1), .in25(1'b0), .in26(1'b1), .in27(1'b0), .in28(1'b0), .in29(1'b0), .in30(1'b0), .in31(1'b0),
    .out(enable), .sel({inst[15:13], inst[1:0]}));
endmodule

module memory_read_enable (
  input  [15:0] inst,
  output enable
);

  Multiplexer #(.select(5)) multiplexer_1 (
    .in0(1'b0), .in1(1'b0), .in2(1'b0), .in3(1'b0), .in4(1'b0), .in5(1'b0), .in6(1'b0), .in7(1'b0),
    .in8(1'b1), .in9(1'b0), .in10(1'b0), .in11(1'b0), .in12(1'b0), .in13(1'b0), .in14(1'b0), .in15(1'b0),
    .in16(1'b0), .in17(1'b0), .in18(1'b0), .in19(1'b0), .in20(1'b0), .in21(1'b0), .in22(1'b0), .in23(1'b0),
    .in24(1'b0), .in25(1'b0), .in26(1'b0), .in27(1'b0), .in28(1'b0), .in29(1'b0), .in30(1'b0), .in31(1'b0),
    .out(enable), .sel({inst[15:13], inst[1:0]}));
endmodule

module memory_data (
  input  [31:0] rs2,
  input  [15:0] inst,
  output [31:0] mem_data
);

  Multiplexer #(.select(5), .width(32)) multiplexer_1 (
    .in0({32{1'b0}}), .in1({32{1'b0}}), .in2({32{1'b0}}), .in3({32{1'b0}}), .in4({32{1'b0}}),
    .in5({32{1'b0}}), .in6({32{1'b0}}), .in7({32{1'b0}}), .in8({32{1'b0}}), .in9({32{1'b0}}),
    .in10({32{1'b0}}), .in11({32{1'b0}}), .in12({32{1'b0}}), .in13({32{1'b0}}), .in14({32{1'b0}}),
    .in15({32{1'b0}}), .in16({32{1'b0}}), .in17({32{1'b0}}), .in18({32{1'b0}}), .in19({32{1'b0}}),
    .in20({32{1'b0}}), .in21({32{1'b0}}), .in22({32{1'b0}}), .in23({32{1'b0}}), .in24(rs2),
    .in25({32{1'b0}}), .in26(rs2), .in27({32{1'b0}}), .in28({32{1'b0}}), .in29({32{1'b0}}),
    .in30({32{1'b0}}), .in31({32{1'b0}}), .out(mem_data), .sel({inst[15:13], inst[1:0]}));
endmodule

module memory_address (
  input  [15:0] inst,
  input  [31:0] alu_result,
  output [31:0] mem_addr
);

  Multiplexer #(.select(5), .width(32)) multiplexer_1 (
    .in0({32{1'b0}}), .in1({32{1'b0}}), .in2({32{1'b0}}), .in3({32{1'b0}}), .in4({32{1'b0}}),
    .in5({32{1'b0}}), .in6({32{1'b0}}), .in7({32{1'b0}}), .in8({32{1'b0}}), .in9({32{1'b0}}),
    .in10({32{1'b0}}), .in11({32{1'b0}}), .in12({32{1'b0}}), .in13({32{1'b0}}), .in14({32{1'b0}}),
    .in15({32{1'b0}}), .in16({32{1'b0}}), .in17({32{1'b0}}), .in18({32{1'b0}}), .in19({32{1'b0}}),
    .in20({32{1'b0}}), .in21({32{1'b0}}), .in22({32{1'b0}}), .in23({32{1'b0}}), .in24(alu_result),
    .in25({32{1'b0}}), .in26(alu_result), .in27({32{1'b0}}), .in28({32{1'b0}}), .in29({32{1'b0}}),
    .in30({32{1'b0}}), .in31({32{1'b0}}), .out(mem_addr), .sel({inst[15:13], inst[1:0]}));

  // Other names for the same wires on the sheet: memory_address[31:0] = mem_addr
endmodule

module pc_write_enable (
  input  [15:0] inst,
  input  [31:0] rs1,
  input  [31:0] rs2,
  output enable
);

  wire comparator_1_eq, comparator_2_eq, multiplexer_1_out, multiplexer_2_out;

  Comparator #(.width(32)) comparator_1 (.a({32{1'b0}}), .b(rs2), .eq(comparator_1_eq));  // open: gt, lt
  Comparator #(.width(32)) comparator_2 (.a({32{1'b0}}), .b(rs1), .eq(comparator_2_eq));  // open: gt, lt
  Multiplexer multiplexer_1 (.in0(1'b0), .in1(1'b1), .out(multiplexer_1_out), .sel(comparator_1_eq));
  Multiplexer multiplexer_2 (.in0(1'b0), .in1(1'b1), .out(multiplexer_2_out), .sel(comparator_2_eq));
  Multiplexer #(.select(5)) multiplexer_3 (
    .in0(1'b0), .in1(1'b0), .in2(1'b0), .in3(1'b0), .in4(1'b0), .in5(1'b0), .in6(1'b0), .in7(1'b0),
    .in8(1'b0), .in9(1'b0), .in10(1'b0), .in11(1'b0), .in12(1'b0), .in13(1'b0), .in14(1'b0), .in15(1'b0),
    .in16(1'b0), .in17(1'b0), .in18(multiplexer_1_out), .in19(1'b0), .in20(1'b0), .in21(1'b1), .in22(1'b0),
    .in23(1'b0), .in24(1'b0), .in25(multiplexer_2_out), .in26(1'b0), .in27(1'b0), .in28(1'b0), .in29(1'b0),
    .in30(1'b0), .in31(1'b0), .out(enable), .sel({inst[15:13], inst[1:0]}));
endmodule

module pc_data (
  input  [15:0] inst,
  input  [31:0] pc_in,
  input  [31:0] data_rs1,
  input  [31:0] data_rs2,
  input  [31:0] data_imm,
  output [31:0] pc_out
);

  wire comparator_1_eq, comparator_2_eq;
  wire [31:0] adder_1_out, adder_2_out, multiplexer_1_out, multiplexer_2_out;

  Adder #(.width(32)) adder_1 (.a(pc_in), .b(data_imm), .out(adder_1_out));  // open: cin, cout
  Comparator #(.width(32)) comparator_1 (.a({32{1'b0}}), .b(data_rs2), .eq(comparator_1_eq));  // open: gt, lt
  Multiplexer #(.width(32)) multiplexer_1 (.in0(pc_in), .in1(data_rs1), .out(multiplexer_1_out), .sel(comparator_1_eq));
  Comparator #(.width(32)) comparator_2 (.a({32{1'b0}}), .b(data_rs1), .eq(comparator_2_eq));  // open: gt, lt
  Multiplexer #(.width(32)) multiplexer_2 (
    .in0(pc_in), .in1(adder_1_out), .out(multiplexer_2_out), .sel(comparator_2_eq));
  Adder #(.width(32)) adder_2 (.a(pc_in), .b(data_imm), .out(adder_2_out));  // open: cin, cout
  Multiplexer #(.select(5), .width(32)) multiplexer_3 (
    .in0(pc_in), .in1(pc_in), .in2(pc_in), .in3(pc_in), .in4(pc_in), .in5(pc_in), .in6(pc_in), .in7(pc_in),
    .in8(pc_in), .in9(pc_in), .in10(pc_in), .in11(pc_in), .in12(pc_in), .in13(pc_in), .in14(pc_in),
    .in15(pc_in), .in16(pc_in), .in17(pc_in), .in18(multiplexer_1_out), .in19(pc_in), .in20(pc_in),
    .in21(adder_2_out), .in22(pc_in), .in23(pc_in), .in24(pc_in), .in25(multiplexer_2_out), .in26(pc_in),
    .in27(pc_in), .in28(pc_in), .in29(pc_in), .in30(pc_in), .in31(pc_in), .out(pc_out),
    .sel({inst[15:13], inst[1:0]}));

  // Other names for the same wires on the sheet: imm[31:0] = data_imm; rs1[31:0] = data_rs1; rs2[31:0] = data_rs2
endmodule
